# Fritzing sketch releSketch (saved by Fritzing 0.9.3b)
breadboards: 1

parts:
  U1 = RELAY [package=relay-jzc]
  U2 = RELAY [package=relay-jzc]
  J1 = Power Jack [package=power_jack_smd]  # not connected
  Componente2 = Arduino Mega 2560 (Rev3)

nets:
  N1: U1.COIL2, U1.NC, U2.COIL2, U2.NC, Componente2.GND
  N2: U1.NO, Componente2.D4_PWM
  N3: U2.NO, Componente2.D5_PWM

notes:
  Fuente de 12v
  Sirena
  Camara IP
